// Logisim project TP1.circ as structural Verilog: 1 circuit, main circuit main
module main (
  input  in_1,
  input  [3:0] in_2,
  input  [3:0] in_3,
  input  in_4,
  input  [31:0] in_5,
  input  [1:0] in_6
);

  wire [31:0] alu_1_sortie, banc_reg_1_valreg1;

  banc_reg banc_reg_1 (
    .clk(in_1), .ValEcriture(alu_1_sortie), .IndReg1(in_2), .IndRegEcr(in_3), .SigEcr(in_4),
    .Valreg1(banc_reg_1_valreg1));  // open: IndReg0, R15_in, ValReg0
  // Probe on banc_reg_1_valreg1
  ALU alu_1 (.Op2(in_5), .Sel(in_6), .Sortie(alu_1_sortie));  // open: Op1, NZCV
endmodule
